// Logisim project DecodeModule.circ as structural Verilog: 3 circuits, main circuit R_decoder
module R_decoder (
  input  [31:0] instruction,
  output [31:0] outp
);

  wire clock_1_out, controllogic_1_registerload;
  wire [3:0] controllogic_1_aluselect;
  wire [4:0] r_splitter_1_rd_i, r_splitter_1_rs1_i, r_splitter_1_rs2_i;
  wire [31:0] registerfile32_1_rs1, registerfile32_1_rs2;

  R_Splitter r_splitter_1 (
    .instruction(instruction), .rd_i(r_splitter_1_rd_i), .rs1_i(r_splitter_1_rs1_i),
    .rs2_i(r_splitter_1_rs2_i));  // open: opcode, funct_3, funct_7
  Clock clock_1 (.out(clock_1_out));
  ControlLogic controllogic_1 (
    .instruction(instruction), .registerLoad(controllogic_1_registerload),
    .ALUselect(controllogic_1_aluselect));
  RegisterFile32 registerfile32_1 (
    .load(controllogic_1_registerload), .rsi1(r_splitter_1_rs1_i), .rsi2(r_splitter_1_rs2_i),
    .rdi(r_splitter_1_rd_i), .rd(outp), .clock(clock_1_out), .rs1(registerfile32_1_rs1),
    .rs2(registerfile32_1_rs2));
  // ALU alu_1: pin names not known; wires that end beside it: controllogic_1_aluselect, registerfile32_1_rs1, registerfile32_1_rs2, outp
endmodule

module ControlLogic (
  input  [31:0] instruction,
  output registerLoad,
  output [3:0] ALUselect
);

  wire and_1_out, and_2_out, and_3_out, and_4_out, and_5_out, and_6_out, and_7_out, and_8_out, and_9_out,
       and_10_out;

  and and_1 (and_1_out, ~instruction[2], ~instruction[3], instruction[4], instruction[5], ~instruction[6], ~instruction[12], ~instruction[13], ~instruction[14], ~instruction[30]);  // AND_Gate
  and and_2 (and_2_out, ~instruction[2], ~instruction[3], instruction[4], instruction[5], ~instruction[6], ~instruction[12], ~instruction[13], ~instruction[14], instruction[30]);  // AND_Gate
  and and_3 (and_3_out, ~instruction[2], ~instruction[3], instruction[4], instruction[5], ~instruction[6], instruction[12], ~instruction[13], ~instruction[14], ~instruction[30]);  // AND_Gate
  and and_4 (and_4_out, ~instruction[2], ~instruction[3], instruction[4], instruction[5], ~instruction[6], ~instruction[12], instruction[13], ~instruction[14], ~instruction[30]);  // AND_Gate
  and and_5 (and_5_out, ~instruction[2], ~instruction[3], instruction[4], instruction[5], ~instruction[6], instruction[12], instruction[13], ~instruction[14], ~instruction[30]);  // AND_Gate
  and and_6 (and_6_out, ~instruction[2], ~instruction[3], instruction[4], instruction[5], ~instruction[6], ~instruction[12], ~instruction[13], instruction[14], ~instruction[30]);  // AND_Gate
  and and_7 (and_7_out, ~instruction[2], ~instruction[3], instruction[4], instruction[5], ~instruction[6], instruction[12], ~instruction[13], instruction[14], ~instruction[30]);  // AND_Gate
  and and_8 (and_8_out, ~instruction[2], ~instruction[3], instruction[4], instruction[5], ~instruction[6], instruction[12], ~instruction[13], instruction[14], instruction[30]);  // AND_Gate
  and and_9 (and_9_out, ~instruction[2], ~instruction[3], instruction[4], instruction[5], ~instruction[6], ~instruction[12], instruction[13], instruction[14], ~instruction[30]);  // AND_Gate
  and and_10 (and_10_out, ~instruction[2], ~instruction[3], instruction[4], instruction[5], ~instruction[6], instruction[12], instruction[13], instruction[14], ~instruction[30]);  // AND_Gate
  or or_1 (registerLoad, and_10_out, and_9_out, and_8_out, and_7_out, and_6_out, and_5_out, and_4_out, and_3_out, and_2_out, and_1_out);
  or or_2 (ALUselect[3], and_2_out, and_8_out);
  or or_3 (ALUselect[2], and_6_out, and_7_out, and_8_out, and_9_out, and_10_out);
  or or_4 (ALUselect[1], and_4_out, and_5_out, and_9_out, and_10_out);
  or or_5 (ALUselect[0], and_3_out, and_5_out, and_7_out, and_8_out, and_10_out);

  // Notes on the sheet:
  //   ADD
  //   SUB
  //   SLL
  //   SLT
  //   XOR
  //   SRL
  //   SRA
  //   OR
  //   AND
  //   SLTU
  //   ALUselect_0
  //   ALUselect_1
  //   ALUselect_2
  //   ALUselect_3
  //   Formulas
  //   ALUselect_0 = SUB  + SRA
  //   ALUselect_2 = SLT + SLTU +OR + AND
  //   ALUselect_1 = XOR + SRL + SRA + OR + AND
  //   ALUselect_3 = SLL + SLTU + SRL + SRA + AND
  //   registerLoad = ADD + SUB + SLL + SLT + SLTU + XOR + SRL + SRA + OR + AND
endmodule

module Clogic (
  input  [31:0] instruction,
  output load
);

  wire a_nd, ADD, o_r, s_ll, s_ra, s_rl, slt, sltu, SUB, x_or;

  and and_1 (ADD, ~instruction[2], ~instruction[3], instruction[4], instruction[5], ~instruction[6], ~instruction[12], ~instruction[13], ~instruction[14], ~instruction[30]);  // AND_Gate
  and and_2 (SUB, ~instruction[2], ~instruction[3], instruction[4], instruction[5], ~instruction[6], ~instruction[12], ~instruction[13], ~instruction[14], instruction[30]);  // AND_Gate
  and and_3 (s_ll, ~instruction[2], ~instruction[3], instruction[4], instruction[5], ~instruction[6], instruction[12], ~instruction[13], ~instruction[14], ~instruction[30]);  // AND_Gate
  and and_4 (slt, ~instruction[2], ~instruction[3], instruction[4], instruction[5], ~instruction[6], ~instruction[12], instruction[13], ~instruction[14], ~instruction[30]);  // AND_Gate
  and and_5 (sltu, ~instruction[2], ~instruction[3], instruction[4], instruction[5], ~instruction[6], instruction[12], instruction[13], ~instruction[14], ~instruction[30]);  // AND_Gate
  and and_6 (x_or, ~instruction[2], ~instruction[3], instruction[4], instruction[5], ~instruction[6], ~instruction[12], ~instruction[13], instruction[14], ~instruction[30]);  // AND_Gate
  and and_7 (s_rl, ~instruction[2], ~instruction[3], instruction[4], instruction[5], ~instruction[6], instruction[12], ~instruction[13], instruction[14], ~instruction[30]);  // AND_Gate
  and and_8 (s_ra, ~instruction[2], ~instruction[3], instruction[4], instruction[5], ~instruction[6], instruction[12], ~instruction[13], instruction[14], instruction[30]);  // AND_Gate
  and and_9 (o_r, ~instruction[2], ~instruction[3], instruction[4], instruction[5], ~instruction[6], ~instruction[12], instruction[13], instruction[14], ~instruction[30]);  // AND_Gate
  and and_10 (a_nd, ~instruction[2], ~instruction[3], instruction[4], instruction[5], ~instruction[6], instruction[12], instruction[13], instruction[14], ~instruction[30]);  // AND_Gate
  or or_1 (load, ADD, SUB, s_ll, slt, sltu, x_or, s_rl, s_ra, o_r, a_nd);

  // Notes on the sheet:
  //   ADD
  //   SUB
  //   SLL
  //   SLT
  //   XOR
  //   SRL
  //   SRA
  //   OR
  //   AND
  //   SLTU
  //   Formulas
  //   ALUselect_0 = SUB  + SRA
  //   ALUselect_2 = SLT + SLTU +OR + AND
  //   ALUselect_1 = XOR + SRL + SRA + OR + AND
  //   ALUselect_3 = SLL + SLTU + SRL + SRA + AND
endmodule
